// Logisim project CircuitoFinal_MarcosAugustoSouzaPinto.circ as structural Verilog: 12 circuits, main circuit Deco_3x8
module main (
);

  wire and_1_out, available, clock_display, clock_teclado, comparator_1_eq, comparator_2_eq, data_addr,
       flag_1_s0, flag_1_s1, flag_1_s2, flag_1_s3, in_out, io_e, or_1_out, re_teclado, uc_1_init, uc_1_ir_s,
       uc_1_to_acc_e, uc_1_to_acc_s, uc_1_to_bus1, uc_1_to_flags_s, uc_1_to_iar_e, uc_1_to_iar_s,
       uc_1_to_mar_s, uc_1_to_r0_e, uc_1_to_r0_s, uc_1_to_r1_e, uc_1_to_r1_s, uc_1_to_r2_e, uc_1_to_r2_s,
       uc_1_to_r3_e, uc_1_to_r3_s, uc_1_to_ram_e, uc_1_to_ram_s, uc_1_to_tmp_s, ula_1_a_igual_b,
       ula_1_a_maior, ula_1_c_out, ula_1_zero, we_display;
  wire [2:0] uc_1_ula_op;
  wire [6:0] data_display, data_teclado;
  wire [7:0] ACC_q, bit_extender_2_out, bus_1_1_saida, controlled_buffer_1_out, IAR_q, IR_q, MAR_q, R0_q,
       R1_q, R2_q, R3_q, ram_1_dout, register_3_q, TMP_q, ula_1_resultado;

  Register TMP (.D(controlled_buffer_1_out), .Q(TMP_q), .clk(uc_1_to_tmp_s));  // open: en, clr
  bus_1 bus_1_1 (.entrada(TMP_q), .saida(bus_1_1_saida), .s(uc_1_to_bus1));
  ULA ula_1 (
    .A(controlled_buffer_1_out), .B(bus_1_1_saida), .resultado(ula_1_resultado), .opCode(uc_1_ula_op),
    .c_out(ula_1_c_out), .a_maior(ula_1_a_maior), .a_igual_b(ula_1_a_igual_b), .zero(ula_1_zero));
  Register ACC (.D(ula_1_resultado), .Q(ACC_q), .clk(uc_1_to_acc_s));  // open: en, clr
  assign controlled_buffer_1_out = uc_1_to_acc_e ? ACC_q : 8'bz;  // Controlled_Buffer controlled_buffer_1
  flag flag_1 (
    .A(ula_1_c_out), .B(ula_1_a_maior), .C(ula_1_a_igual_b), .D(ula_1_zero), .s0(flag_1_s0), .s1(flag_1_s1),
    .s2(flag_1_s2), .s3(flag_1_s3), .flag_s(uc_1_to_flags_s));
  TTY tty_1 (.data(data_display), .clk(clock_display), .we(we_display));  // open: clr
  Keyboard #(.buflen(45)) keyboard_1 (
    .clk(clock_teclado), .re(re_teclado), .avail(available), .data(data_teclado));  // open: clr
  assign controlled_buffer_1_out = uc_1_to_r0_e ? R0_q : 8'bz;  // Controlled_Buffer controlled_buffer_2
  Register R0 (.D(controlled_buffer_1_out), .Q(R0_q), .clk(uc_1_to_r0_s));  // open: en, clr
  Register IAR (.D(controlled_buffer_1_out), .Q(IAR_q), .clk(uc_1_to_iar_s));  // open: en, clr
  assign controlled_buffer_1_out = uc_1_to_iar_e ? IAR_q : 8'bz;  // Controlled_Buffer controlled_buffer_3
  assign controlled_buffer_1_out = uc_1_to_r1_e ? R1_q : 8'bz;  // Controlled_Buffer controlled_buffer_4
  Register R1 (.D(controlled_buffer_1_out), .Q(R1_q), .clk(uc_1_to_r1_s));  // open: en, clr
  Register IR (.D(controlled_buffer_1_out), .Q(IR_q), .clk(uc_1_ir_s));  // open: en, clr
  UC uc_1 (
    .ULA_op(uc_1_ula_op), .from_carry_out(flag_1_s0), .from_larger(flag_1_s1), .from_equal(flag_1_s2),
    .from_zero(flag_1_s3), .to_flags_s(uc_1_to_flags_s), .to_bus1(uc_1_to_bus1), .to_TMP_s(uc_1_to_tmp_s),
    .to_R0_s(uc_1_to_r0_s), .to_R0_e(uc_1_to_r0_e), .to_R1_s(uc_1_to_r1_s), .to_R1_e(uc_1_to_r1_e),
    .to_R2_s(uc_1_to_r2_s), .to_R2_e(uc_1_to_r2_e), .to_R3_s(uc_1_to_r3_s), .to_R3_e(uc_1_to_r3_e),
    .to_MAR_S(uc_1_to_mar_s), .to_ACC_s(uc_1_to_acc_s), .to_ACC_e(uc_1_to_acc_e), .to_IAR_s(uc_1_to_iar_s),
    .to_IAR_e(uc_1_to_iar_e), .IR_input(IR_q), .IR_s(uc_1_ir_s), .input_output(in_out),
    .data_address(data_addr), .to_IO_e(io_e), .to_IO_s(clock_display), .to_RAM_s(uc_1_to_ram_s),
    .to_RAM_e(uc_1_to_ram_e), .init(uc_1_init));
  LED led_1 (.in(uc_1_init));
  and and_1 (and_1_out, clock_display, data_addr, in_out);
  assign controlled_buffer_1_out = uc_1_to_r2_e ? R2_q : 8'bz;  // Controlled_Buffer controlled_buffer_5
  Register R2 (.D(controlled_buffer_1_out), .Q(R2_q), .clk(uc_1_to_r2_s));  // open: en, clr
  assign controlled_buffer_1_out = uc_1_to_r3_e ? R3_q : 8'bz;  // Controlled_Buffer controlled_buffer_6
  Register R3 (.D(controlled_buffer_1_out), .Q(R3_q), .clk(uc_1_to_r3_s));  // open: en, clr
  T_Flip_Flop t_ff_1 (.clk(io_e), .T(available), .Q(clock_teclado));  // open: Qn, preset, reset
  Comparator comparator_1 (.a(controlled_buffer_1_out), .b(8'h97), .eq(comparator_1_eq));  // open: gt, lt
  Register MAR (.D(controlled_buffer_1_out), .Q(MAR_q), .clk(uc_1_to_mar_s));  // open: en, clr
  or or_1 (or_1_out, uc_1_to_ram_s, uc_1_to_ram_e);
  Register #(.width(1)) register_1 (.D(comparator_1_eq), .Q(re_teclado), .clk(and_1_out));  // open: en, clr
  Bit_Extender #(.out_width(7), .\type ("zero")) bit_extender_1 (.in(controlled_buffer_1_out), .out(data_display));
  Comparator comparator_2 (.a(controlled_buffer_1_out), .b(8'h98), .eq(comparator_2_eq));  // open: gt, lt
  Register #(.width(1)) register_2 (.D(comparator_2_eq), .Q(we_display), .clk(and_1_out));  // open: en, clr
  RAM #(.\type ("nonvolatile")) ram_1 (
    .addr(MAR_q), .we(uc_1_to_ram_s), .oe(uc_1_to_ram_e), .clk(or_1_out), .din(controlled_buffer_1_out),
    .dout(ram_1_dout));
  assign bit_extender_2_out = {{1{1'b0}}, data_teclado};  // Bit_Extender bit_extender_2
  Register register_3 (.D(bit_extender_2_out), .Q(register_3_q), .clk(clock_teclado));  // open: en, clr
  assign controlled_buffer_1_out = io_e ? register_3_q : 8'bz;  // Controlled_Buffer controlled_buffer_7
  assign controlled_buffer_1_out = uc_1_to_ram_e ? ram_1_dout : 8'bz;  // Controlled_Buffer controlled_buffer_8

  // Other names for the same wires on the sheet: io_s = clock_display
endmodule

module Deco_3x8 (
  input  A,
  input  B,
  input  C,
  output s0,
  output s1,
  output s2,
  output s3,
  output s4,
  output s5,
  output s6,
  output s7
);

  wire not_1_out, not_2_out, not_3_out;

  not not_1 (not_1_out, C);
  not not_2 (not_2_out, B);
  not not_3 (not_3_out, A);
  and and_1 (s0, not_3_out, not_2_out, not_1_out);
  and and_2 (s1, not_3_out, not_2_out, C);
  and and_3 (s2, not_3_out, B, not_1_out);
  and and_4 (s3, not_3_out, B, C);
  and and_5 (s4, A, not_2_out, not_1_out);
  and and_6 (s5, A, not_2_out, C);
  and and_7 (s6, A, B, not_1_out);
  and and_8 (s7, A, C, B);
endmodule

module SHL (
  input  c_in,
  input  [7:0] entrada,
  output [7:0] saida_SHL,
  output c_out
);


  assign c_out = entrada[7];
  assign saida_SHL = {entrada[6:0], c_in};
endmodule

module ULA (
  input  [2:0] opCode,
  input  [7:0] A,
  input  [7:0] B,
  output c_out,
  output [7:0] resultado,
  output a_maior,
  output a_igual_b,
  output zero
);

  wire adder_1_cout, left_c_out, or_2_out, right_c_out;
  wire [7:0] adder_1_out, and_1_out, left_saida_shl, not_1_out, or_1_out, right_saida_shr, xor_1_out;

  Adder adder_1 (.a(A), .b(B), .out(adder_1_out), .cin(1'b0), .cout(adder_1_cout));
  SHR right (.entrada(A), .c_in(1'b0), .c_out(right_c_out), .saida_SHR(right_saida_shr));
  SHL left (.entrada(A), .c_in(1'b0), .c_out(left_c_out), .saida_SHL(left_saida_shl));
  assign not_1_out = ~A;  // NOT_Gate not_1, 8 bits wide
  assign and_1_out = A & B;  // AND_Gate and_1, 8 bits wide
  assign or_1_out = A | B;  // OR_Gate or_1, 8 bits wide
  assign xor_1_out = A ^ B;  // XOR_Gate xor_1, 8 bits wide
  Comparator comparator_1 (.a(A), .b(B), .gt(a_maior), .eq(a_igual_b));  // open: lt
  Multiplexer #(.select(3), .width(8)) multiplexer_1 (
    .in0(adder_1_out), .in1(right_saida_shr), .in2(left_saida_shl), .in3(not_1_out), .in4(and_1_out),
    .in5(or_1_out), .in6(xor_1_out), .in7(A), .out(resultado), .sel(opCode));
  Multiplexer #(.select(3)) multiplexer_2 (
    .in0(adder_1_cout), .in1(right_c_out), .in2(left_c_out), .in3(1'b0), .in4(1'b0), .in5(1'b0), .in6(1'b0),
    .in7(1'b0), .out(c_out), .sel(opCode));
  or or_2 (or_2_out, resultado[0], resultado[1], resultado[2], resultado[3], resultado[4], resultado[5], resultado[6], resultado[7]);
  not not_2 (zero, or_2_out);
endmodule

module SHR (
  input  c_in,
  input  [7:0] entrada,
  output [7:0] saida_SHR,
  output c_out
);


  assign c_out = entrada[0];
  assign saida_SHR = {c_in, entrada[7:1]};
endmodule

// clk
module CLK (
  output clk_s,
  output main,
  output clk_e
);

  wire clk_d_out;

  Clock #(.highDuration(2), .lowDuration(2)) main_clk (.out(main));
  Clock #(.highDuration(2), .lowDuration(2), .phaseOffset(3)) clk_d (.out(clk_d_out));
  or or_1 (clk_e, main, clk_d_out);
  and and_1 (clk_s, clk_d_out, main);
endmodule

module stepper (
  input  e,
  output s0,
  output s1,
  output s2,
  output s3,
  output s4,
  output s5,
  output s6
);

  wire decoder_1_out7;
  wire [2:0] counter_1_q;

  Counter #(.max('h7), .width(3)) counter_1 (
    .Q(counter_1_q), .clk(e), .clr(decoder_1_out7));  // open: load, D, count, carry, up
  Decoder #(.enable("false"), .select(3)) decoder_1 (
    .out0(s0), .out1(s1), .out2(s2), .out3(s3), .out4(s4), .out5(s5), .out6(s6), .out7(decoder_1_out7),
    .sel(counter_1_q));
endmodule

module UC (
  input  from_carry_out,
  input  from_larger,
  input  from_equal,
  input  from_zero,
  input  [7:0] IR_input,
  output to_bus1,
  output to_TMP_s,
  output to_R0_s,
  output to_R0_e,
  output to_R1_s,
  output to_R1_e,
  output to_R2_s,
  output to_R2_e,
  output to_R3_s,
  output to_R3_e,
  output to_MAR_S,
  output [2:0] ULA_op,
  output to_RAM_s,
  output to_RAM_e,
  output init,
  output to_flags_s,
  output data_address,
  output to_IO_e,
  output to_IO_s,
  output input_output,
  output IR_s,
  output to_ACC_s,
  output to_ACC_e,
  output to_IAR_e,
  output to_IAR_s
);

  wire A_out, and_8_out, and_9_out, and_10_out, and_11_out, and_12_out, and_13_out, and_14_out, and_15_out,
       and_16_out, and_17_out, and_18_out, and_19_out, and_20_out, and_21_out, and_22_out, and_23_out,
       and_24_out, and_25_out, and_26_out, and_27_out, and_28_out, and_29_out, and_30_out, and_31_out,
       and_32_out, and_33_out, and_34_out, and_35_out, C_out, clk_1_main, clk_e, clk_s, deco_2x4_1_s0,
       deco_2x4_1_s1, deco_2x4_1_s2, deco_2x4_1_s3, deco_3x8_1_s0, deco_3x8_1_s1, deco_3x8_1_s2,
       deco_3x8_1_s3, deco_3x8_1_s4, deco_3x8_1_s5, deco_3x8_1_s6, deco_3x8_1_s7, E_out, not_1_out,
       not_2_out, not_3_out, or_2_out, or_3_out, or_4_out, or_5_out, or_6_out, or_7_out, or_8_out, or_9_out,
       or_10_out, or_11_out, or_12_out, s1, s2, s3, s4, s5, s6, Z_out;

  CLK clk_1 (.clk_s(clk_s), .main(clk_1_main), .clk_e(clk_e));
  and and_1 (to_IAR_e, or_2_out, clk_e);
  and and_2 (to_RAM_e, or_3_out, clk_e);
  and and_3 (to_ACC_e, or_4_out, clk_e);
  and and_4 (to_IO_e, and_32_out, clk_e);
  Enable_Reg enable_reg_1 (
    .s0(to_R0_e), .s1(to_R1_e), .s2(to_R2_e), .s3(to_R3_e), .A(clk_e), .B(or_5_out), .C(or_6_out),
    .entrada_A(IR_input[0]), .entrada_B(IR_input[1]), .entr_A(IR_input[2]), .entr_B(IR_input[3]));
  or or_1 (to_bus1, s1, and_24_out, and_23_out, and_20_out);
  or or_2 (or_2_out, s1, and_20_out, and_22_out, and_23_out);
  or or_3 (or_3_out, s2, and_30_out, and_35_out, and_29_out, and_27_out);
  or or_4 (or_4_out, s3, and_31_out, and_34_out, and_33_out);
  or or_5 (or_5_out, and_17_out, and_28_out, and_21_out, and_25_out);
  or or_6 (or_6_out, and_19_out, and_18_out, and_26_out);
  and and_5 (ULA_op[0], s5, IR_input[7], IR_input[4]);
  and and_6 (ULA_op[1], s5, IR_input[7], IR_input[5]);
  and and_7 (ULA_op[2], s5, IR_input[7], IR_input[6]);
  not not_1 (not_1_out, IR_input[7]);
  Deco_3x8 deco_3x8_1 (
    .A(IR_input[6]), .B(IR_input[5]), .C(IR_input[4]), .s0(deco_3x8_1_s0), .s1(deco_3x8_1_s1),
    .s2(deco_3x8_1_s2), .s3(deco_3x8_1_s3), .s4(deco_3x8_1_s4), .s5(deco_3x8_1_s5), .s6(deco_3x8_1_s6),
    .s7(deco_3x8_1_s7));
  stepper stepper_1 (.e(clk_1_main), .s1(s1), .s2(s2), .s3(s3), .s4(s4), .s5(s5), .s6(s6), .s0(init));
  and and_8 (and_8_out, IR_input[4], IR_input[5], IR_input[6]);
  and and_9 (and_9_out, not_1_out, deco_3x8_1_s0);
  and and_10 (and_10_out, not_1_out, deco_3x8_1_s1);
  and and_11 (and_11_out, not_1_out, deco_3x8_1_s2);
  and and_12 (and_12_out, not_1_out, deco_3x8_1_s3);
  and and_13 (and_13_out, not_1_out, deco_3x8_1_s4);
  and and_14 (and_14_out, not_1_out, deco_3x8_1_s5);
  and and_15 (and_15_out, not_1_out, deco_3x8_1_s6);
  and and_16 (and_16_out, not_1_out, deco_3x8_1_s7);
  and and_17 (and_17_out, s4, IR_input[7]);
  and and_18 (and_18_out, s4, and_9_out);
  and and_19 (and_19_out, s4, and_10_out);
  and and_20 (and_20_out, s4, and_11_out);
  and and_21 (and_21_out, s4, and_12_out);
  and and_22 (and_22_out, s4, and_13_out);
  and and_23 (and_23_out, s4, and_14_out);
  and and_24 (and_24_out, s4, and_15_out);
  and and_25 (and_25_out, s4, and_16_out, IR_input[3]);
  not not_2 (not_2_out, and_8_out);
  not not_3 (not_3_out, IR_input[3]);
  and C (C_out, IR_input[3], from_carry_out);
  and A (A_out, IR_input[2], from_larger);
  and E (E_out, IR_input[1], from_equal);
  and Z (Z_out, IR_input[0], from_zero);
  and and_26 (and_26_out, s5, IR_input[7]);
  and and_27 (and_27_out, s5, and_9_out);
  and and_28 (and_28_out, s5, and_10_out);
  and and_29 (and_29_out, s5, and_11_out);
  and and_30 (and_30_out, s5, and_13_out);
  and and_31 (and_31_out, s5, and_14_out);
  and and_32 (and_32_out, s5, and_16_out, not_3_out);
  or or_7 (or_7_out, C_out, A_out, E_out, Z_out);
  and and_33 (and_33_out, s6, IR_input[7], not_2_out);
  and and_34 (and_34_out, s6, and_11_out);
  and and_35 (and_35_out, s6, and_14_out, or_7_out);
  or or_8 (or_8_out, s3, and_21_out, and_30_out, and_31_out, and_34_out, and_35_out);
  or or_9 (or_9_out, s1, and_20_out, and_23_out, and_26_out);
  or or_10 (or_10_out, and_24_out, and_26_out);
  or or_11 (or_11_out, and_27_out, and_33_out, and_29_out, and_32_out);
  deco_2X4 deco_2x4_1 (
    .A(IR_input[0]), .B(IR_input[1]), .s0(deco_2x4_1_s0), .s1(deco_2x4_1_s1), .s2(deco_2x4_1_s2),
    .s3(deco_2x4_1_s3));
  or or_12 (or_12_out, s1, and_20_out, and_23_out, and_18_out, and_19_out, and_22_out);
  and and_36 (IR_s, s2, clk_s);
  and and_37 (to_MAR_S, or_12_out, clk_s);
  and and_38 (to_IAR_s, clk_s, or_8_out);
  and and_39 (to_ACC_s, clk_s, or_9_out);
  and and_40 (to_RAM_s, and_28_out, clk_s);
  and and_41 (to_TMP_s, clk_s, and_17_out);
  and and_42 (to_flags_s, clk_s, or_10_out);
  and and_43 (to_IO_s, and_25_out, clk_s);
  and and_44 (to_R0_s, or_11_out, clk_s, deco_2x4_1_s0);
  and and_45 (to_R1_s, clk_s, or_11_out, deco_2x4_1_s1);
  and and_46 (to_R2_s, clk_s, or_11_out, deco_2x4_1_s2);
  and and_47 (to_R3_s, or_11_out, clk_s, deco_2x4_1_s3);

  assign data_address = IR_input[2];
  assign input_output = IR_input[3];

  // Other names for the same wires on the sheet: from_IR[7:0] = IR_input; Data_Adress = IR_input[2];
  //   to_ULA[2:0] = ULA_op
endmodule

module bus_1 (
  input  [7:0] entrada,
  input  s,
  output [7:0] saida
);

  Multiplexer #(.width(8)) multiplexer_1 (.in0(entrada), .in1(8'h1), .out(saida), .sel(s));
endmodule

module flag (
  input  A,
  input  B,
  input  C,
  input  D,
  input  flag_s,
  output s0,
  output s1,
  output s2,
  output s3
);

  Register #(.width(4)) register_1 (.D({D, C, B, A}), .Q({s3, s2, s1, s0}), .clk(flag_s));  // open: en, clr
endmodule

// R_enable
module Enable_Reg (
  input  A,
  input  B,
  input  C,
  input  entrada_A,
  input  entrada_B,
  input  entr_A,
  input  entr_B,
  output s0,
  output s1,
  output s2,
  output s3
);

  wire and_1_out, and_2_out, and_3_out, and_4_out, and_5_out, and_6_out, and_7_out, and_8_out, deco_2x4_1_s0,
       deco_2x4_1_s1, deco_2x4_1_s2, deco_2x4_1_s3, deco_2x4_2_s0, deco_2x4_2_s1, deco_2x4_2_s2,
       deco_2x4_2_s3;

  or or_1 (s0, and_1_out, and_5_out);
  or or_2 (s1, and_2_out, and_6_out);
  or or_3 (s2, and_3_out, and_7_out);
  or or_4 (s3, and_4_out, and_8_out);
  and and_1 (and_1_out, A, B, deco_2x4_2_s0);
  and and_2 (and_2_out, A, B, deco_2x4_2_s1);
  and and_3 (and_3_out, A, B, deco_2x4_2_s2);
  and and_4 (and_4_out, A, B, deco_2x4_2_s3);
  and and_5 (and_5_out, A, C, deco_2x4_1_s0);
  and and_6 (and_6_out, A, C, deco_2x4_1_s1);
  and and_7 (and_7_out, A, C, deco_2x4_1_s2);
  and and_8 (and_8_out, A, C, deco_2x4_1_s3);
  deco_2X4 deco_2x4_1 (
    .A(entr_A), .B(entr_B), .s0(deco_2x4_1_s0), .s1(deco_2x4_1_s1), .s2(deco_2x4_1_s2), .s3(deco_2x4_1_s3));
  deco_2X4 deco_2x4_2 (
    .A(entrada_A), .B(entrada_B), .s0(deco_2x4_2_s0), .s1(deco_2x4_2_s1), .s2(deco_2x4_2_s2),
    .s3(deco_2x4_2_s3));
endmodule

module deco_2X4 (
  input  A,
  input  B,
  output s0,
  output s1,
  output s2,
  output s3
);

  wire not_1_out, not_2_out;

  not not_1 (not_1_out, A);
  not not_2 (not_2_out, B);
  and and_1 (s0, not_1_out, not_2_out);
  and and_2 (s1, A, not_2_out);
  and and_3 (s2, not_1_out, B);
  and and_4 (s3, A, B);
endmodule
